# Fritzing sketch intro (saved by Fritzing 0.9.5d)
circuit board: 8.46667cm x 5.64444cm
breadboards: 1

parts:
  Part1 = Arduino Nano (Rev3.0)
  LED1 = RGB LED (com. cathode, rgb) [package="5 mm [THT]"]
  R1 = Resistor [tolerance=±5% resistance=220 package=THT]

nets (from the breadboard view):
  N1: Part1.GND, LED1.common_cathode
  N2: Part1.3V3, R1.Pin_0
  N3: LED1.red_anode, R1.Pin_1
