# Fritzing sketch buzzer (saved by Fritzing 0.9.5d)
breadboards: 1

parts:
  J2 = Piezo Speaker
  Part2 = Arduino Nano (Rev3.0)
  R2 = Resistor [tolerance=±5% resistance=100 package=THT]

nets:
  N1: J2.pin1, Part2.GND
  N2: J2.pin2, R2.Pin_1
  N3: Part2.D3, R2.Pin_0
