# Fritzing sketch music_game (saved by Fritzing 0.9.5d)
breadboards: 1

parts:
  Part2 = Arduino Nano (Rev3.0)
  LED2 = RGB LED (com. cathode, rgb) [package="5 mm [THT]"]
  R1 = Resistor [tolerance=±5% resistance=470 package=THT]
  R2 = Resistor [tolerance=±5% resistance=470 package=THT]
  R3 = Resistor [tolerance=±5% resistance=470 package=THT]

nets:
  N1: Part2.GND, LED2.green_anode
  N2: Part2.D4, R2.Pin_1
  N3: Part2.D5, R3.Pin_1
  N4: Part2.D6, R1.Pin_1
  N5: LED2.red_anode, R2.Pin_0
  N6: LED2.common_cathode, R3.Pin_0
  N7: LED2.blue_anode, R1.Pin_0
